# Fritzing sketch sensor_platform (saved by Fritzing 0.9.3b)
circuit board: 10cm x 6cm
breadboards: 1

parts:
  R1 = Resistor [tolerance=±5% resistance=1k package=THT]
  S1 = SWITCH-MOMENTARY-2 [package=tactile_switch_tall]
  R2 = Temperature Sensor (Thermistor) [thermistor_type=NTC package=THT]
  U1 = NodeMCU V3.0
  BMP280_I2C = BMP280 Breakout Board [part_number=BMP280]
  BMP280_SPI = BMP280 Breakout Board [part_number=BMP280]
  J2 = male pin header, 15 pins [form="♂ (male)"]
  DHT1 = DHT11 Humitidy and Temperature Sensor
  R3 = Resistor [tolerance=±5% resistance=1k package=THT]
  J1 = male pin header, 15 pins [form="♂ (male)"]

nets:
  DIGITAL: R1.Pin_0, S1.2, U1.D3, J1.pin4
  VCC: R1.Pin_1, U1.3V3, BMP280_I2C.VCC, BMP280_I2C.CSB, BMP280_I2C.SDO, BMP280_SPI.VCC, J2.pin11, DHT1.VDD, DHT1.NULL, R3.Pin_1, J1.pin6, J1.pin15
  GND: S1.1, R2.pin_1, U1.GND#6, U1.GND#13, U1.GND#16, U1.GND#33, BMP280_I2C.GND, BMP280_SPI.GND, J2.pin10, J2.pin14, DHT1.GND, J1.pin7, J1.pin14
  ANALOG: R2.pin_0, U1.A0, J2.pin1, R3.Pin_0
  N1: U1.D0, J1.pin1
  SCL: U1.D1, BMP280_I2C.SCL, J1.pin2
  SDA: U1.D2, BMP280_I2C.SDA, J1.pin3
  N2: U1.D4, J1.pin5
  SCK: U1.D5, BMP280_SPI.SCL, J1.pin8
  MISO: U1.D6, BMP280_SPI.SDO, J1.pin9
  MOSI: U1.D7, BMP280_SPI.SDA, J1.pin10
  N3: U1.D8, J1.pin11
  SINGLE WIRE: U1.RX, DHT1.DATA, J1.pin12
  N4: U1.TX, J1.pin13
  N5: U1.Vin, J2.pin15
  N6: U1.RST, J2.pin13
  N7: U1.EN, J2.pin12
  N8: U1.SK, J2.pin9
  N9: U1.S0, J2.pin8
  N10: U1.SC, J2.pin7
  N11: U1.S1, J2.pin6
  N12: U1.S2, J2.pin5
  CS: U1.S3, BMP280_SPI.CSB, J2.pin4
  N13: U1.VU, J2.pin3
  N14: U1.GND#41, J2.pin2

notes:
  button with digital signal
  st1147 thermistor analog
  nodemcu
  DHT11 single wire
  BMP280 SPI
  BMP280 I2C

custom parts:
  NodeMCU V3.0: ESP8266 based NodeMCU
  BMP280 Breakout Board: This is a breakout board for the Bosch Sensortec BMP280, "an absolute barometric pressure sensor especially designed for mobile applications." The operation range is 300 to 1100 hPa. Supply voltage is 1.2 to 3.6V. Operating temperature range is -40 to +85 °C.
  DHT11 Humitidy and Temperature Sensor: DHT11 Humidity and Temperature Sensor
